# Fritzing sketch Adafruit_DHT11 (saved by Fritzing 0.9.3b)
breadboards: 1

parts:
  DHT1 = DHT11 Humitidy and Temperature Sensor
  Mod1 = Amica NodeMCU DevKit 1.0
  LED1 = LED - 5mm [color="Green (555nm)" package="5 mm [THT]"]

nets:
  N1: DHT1.VDD, Mod1.pin1, Mod1.pin_10, Mod1.pin_26
  N2: DHT1.DATA, Mod1.pin_13
  N3: DHT1.GND, Mod1.pin2, Mod1.pin_9, Mod1.pin_25, Mod1.pin_29, LED1.cathode
  N4: Mod1.pin_12, LED1.anode

custom parts:
  DHT11 Humitidy and Temperature Sensor: DHT11 Humidity and Temperature Sensor
  Amica NodeMCU DevKit 1.0: Amica NodeMCU DevKit 1.0 Development Kit based on ESP8266 ESP-12E, integating GPIO, PWM, IIC, 1-Wire and ADC all in one board. Links: NodeMCU information page Github
